// Logisim project Assignment2.circ as structural Verilog
module main (
);


  // Notes on the sheet:
  //   TCSS371 Assignment 2
  //   Raiden H
endmodule

module Problem1A (
  input  S3,
  input  S2,
  input  S1,
  input  S0,
  input  A,
  input  B,
  input  C,
  input  D,
  input  E,
  input  F,
  input  G,
  input  H,
  input  I,
  input  J,
  output O
);

  wire and_1_out, and_2_out, and_3_out, and_4_out, and_5_out, and_6_out, and_7_out, and_8_out, and_9_out,
       and_10_out;

  and and_1 (and_1_out, A, ~S0, ~S1, ~S2, ~S3);  // AND_Gate
  and and_2 (and_2_out, B, S0, ~S1, ~S2, ~S3);  // AND_Gate
  and and_3 (and_3_out, C, ~S0, S1, ~S2, ~S3);  // AND_Gate
  and and_4 (and_4_out, D, S0, S1, ~S2, ~S3);  // AND_Gate
  and and_5 (and_5_out, E, ~S0, ~S1, S2, ~S3);  // AND_Gate
  and and_6 (and_6_out, F, S0, ~S1, S2, ~S3);  // AND_Gate
  and and_7 (and_7_out, G, ~S0, S1, S2, ~S3);  // AND_Gate
  and and_8 (and_8_out, H, S0, S1, S2, ~S3);  // AND_Gate
  and and_9 (and_9_out, I, ~S0, ~S1, ~S2, S3);  // AND_Gate
  and and_10 (and_10_out, J, S0, ~S1, ~S2, S3);  // AND_Gate
  or or_1 (O, and_1_out, and_2_out, and_3_out, and_4_out, and_5_out, and_6_out, and_7_out, and_8_out, and_9_out, and_10_out);

  // Notes on the sheet:
  //   0000
  //   0001
  //   0010
  //   0011
  //   0100
  //   0101
  //   0110
  //   0111
  //   1000
  //   1001
  //   8
  //   10-to-1 MUX with only AND, OR, and NOT. Label I/O and provide a truth table.
  //   4
  //   2
  //   1
  //   Supports selectors from 0000 to 1001
  //   S3 is the most significant bit, S0 is the least
  //   TRUTH TABLE
  //   S3  |  S2  |  S1  |  S0  |  OUT
  //   0   |   0   |   0   |   0   |   A
  //   0   |   0   |   0   |   1   |   B
  //   0   |   0   |   1   |   0   |   C
  //   0   |   0   |   1   |   1   |   D
  //   0   |   1   |   0   |   0   |   E
  //   0   |   1   |   0   |   1   |   F
  //   0   |   1   |   1   |   0   |   G
  //   0   |   1   |   1   |   1   |   H
  //   1   |   0   |   0   |   0   |   I
  //   1   |   0   |   0   |   1   |   J
  //   1   |   0   |   1   |   0   |   0
  //   1   |   0   |   1   |   1   |   0
endmodule

module Problem1B (
  input  [7:0] A,
  input  [7:0] B,
  input  Cin,
  output O,
  output Cout
);


  // Notes on the sheet:
  //   8-bit full adder with only AND, OR, and NOT. Label I/O.
endmodule

module Problem1C (
);


  // Notes on the sheet:
  //   8-bit D-Latch using only AND, OR, and NOT. Label I/O
endmodule

module Problem2 (
  input  A,
  input  B,
  input  C,
  input  D,
  output O
);

  wire and_1_out, and_2_out, and_3_out, and_4_out, and_5_out, and_6_out, and_7_out;

  and and_1 (and_1_out, D, C, ~B, ~A);  // AND_Gate
  and and_2 (and_2_out, D, ~C, B, ~A);  // AND_Gate
  and and_3 (and_3_out, ~D, C, B, ~A);  // AND_Gate
  and and_4 (and_4_out, D, ~C, ~B, A);  // AND_Gate
  or or_1 (O, and_1_out, and_2_out, and_3_out, and_4_out, and_5_out, and_6_out, and_7_out);
  and and_5 (and_5_out, ~D, C, ~B, A);  // AND_Gate
  and and_6 (and_6_out, ~D, ~C, B, A);  // AND_Gate
  and and_7 (and_7_out, D, C, B, A);

  // Notes on the sheet:
  //   8
  //   4
  //   2
  //   1
  //   4-bit input, output 1 if input is divisible by 3 or 5 when converted to decimal. Provide a truth table not in the .circ.
endmodule

module Problem3 (
);


  // Notes on the sheet:
  //   design a 4-bit ALU, 3 select lines for 8 operations, 2 input bits + the carry, 1 output + carry. provide a truth table for the available functions
endmodule

module OneBitAdder (
  input  A,
  input  B,
  input  Cin,
  output O,
  output Cout
);

  wire and_1_out, and_2_out, and_3_out, and_4_out, and_5_out, and_6_out, and_7_out;

  and and_1 (and_1_out, Cin, B, A);
  and and_2 (and_2_out, Cin, ~B, ~A);  // AND_Gate
  and and_3 (and_3_out, ~Cin, B, ~A);  // AND_Gate
  and and_4 (and_4_out, ~Cin, ~B, A);  // AND_Gate
  and and_5 (and_5_out, ~Cin, B, A);  // AND_Gate
  and and_6 (and_6_out, Cin, ~B, A);  // AND_Gate
  and and_7 (and_7_out, Cin, B, ~A);  // AND_Gate
  or or_1 (O, and_1_out, and_2_out, and_3_out, and_4_out);
  or or_2 (Cout, and_1_out, and_5_out, and_6_out, and_7_out);
endmodule
